// Logisim project Processor.circ as structural Verilog: 7 circuits, main circuit main
module main (
  input  [3:0] in_1,
  input  [3:0] in_2,
  input  [3:0] in_3,
  input  [3:0] in_4
);

  wire clock_1_out, clock_2_out, clock_3_out, Enable_enabler, register_write_decoder_1_write_enable, ZF;
  wire [3:0] icode, ifun, rA_q, rB_q, register_write_decoder_1_register;
  wire [7:0] alu_1_out_6, register_file_1_out_8, register_file_1_out_9, register_write_decoder_1_write_data,
       undriven, val_A_q, val_B_q, val_C, val_E_q, Val_M, val_M_t, val_P, write_back_1_out_6;

  Register #(.width(4)) u_icode (.D(in_1), .Q(icode), .clk(clock_1_out));  // open: en, clr
  Register #(.width(4)) u_ifun (.D(in_2), .Q(ifun), .clk(clock_1_out));  // open: en, clr
  Register #(.width(4)) rA (.D(in_3), .Q(rA_q), .clk(clock_1_out));  // open: en, clr
  Write_Back write_back_1 (
    .in_1(val_P), .in_2(val_M_t), .in_3(val_C), .icode(icode), .cnd(ZF), .out_6(write_back_1_out_6));
  Register u_val_C (.D(undriven), .Q(val_C), .clk(clock_1_out));  // open: en, clr
  Register #(.width(4)) rB (.D(in_4), .Q(rB_q), .clk(clock_1_out));  // open: en, clr
  Memory Memory (.Address_Bus(val_E_q), .in_2(val_A_q), .Data_Bus(Val_M), .icode(icode));
  Clock clock_1 (.out(clock_1_out));
  ALU alu_1 (
    .out_7(ZF), .icode(icode), .out_6(alu_1_out_6), .val_C(val_C), .val_A(val_A_q), .val_B(val_B_q),
    .ifun(ifun));
  Register val_E (.D(alu_1_out_6), .en(icode[3]), .Q(val_E_q), .clk(clock_2_out));  // open: clr
  Clock clock_2 (.out(clock_2_out));
  Val_A_B_enabler Enable (.icode(icode), .enabler(Enable_enabler));
  Register val_A (.D(register_file_1_out_8), .en(Enable_enabler), .Q(val_A_q), .clk(clock_3_out));  // open: clr
  Register_File register_file_1 (
    .in_5(register_write_decoder_1_write_data), .in_6(register_write_decoder_1_write_enable),
    .in_7(register_write_decoder_1_register), .out_8(register_file_1_out_8), .in_1(Enable_enabler),
    .in_2(rA_q), .out_9(register_file_1_out_9), .in_3(Enable_enabler), .in_4(rB_q));
  Register val_B (.D(register_file_1_out_9), .en(Enable_enabler), .Q(val_B_q), .clk(clock_3_out));  // open: clr
  Clock clock_3 (.out(clock_3_out));
  Register_Write_Decoder register_write_decoder_1 (
    .val_M(val_M_t), .val_E(val_E_q), .val_A(val_A_q), .val_C(val_C),
    .register(register_write_decoder_1_register), .write_data(register_write_decoder_1_write_data),
    .icode(icode), .rA(rA_q), .rB(rB_q), .write_enable(register_write_decoder_1_write_enable));
endmodule

module ALU (
  input  [3:0] ifun,
  input  [7:0] val_B,
  input  [7:0] val_C,
  input  [7:0] val_A,
  input  [3:0] icode,
  output [7:0] out_6,
  output out_7
);

  wire add_out, clock_1_out, ld_out, mul_out, nor_1_out, not_1_out, not_2_out, not_3_out, not_4_out,
       not_5_out, or_1_out, st_out, val_A_out;
  wire [7:0] adder_1_out, multiplexer_2_out, multiplier_1_out;

  and ld (ld_out, icode[3], icode[2], not_1_out, icode[0]);
  not not_1 (not_1_out, icode[1]);
  and st (st_out, icode[3], icode[2], icode[1], not_2_out);
  not not_2 (not_2_out, icode[0]);
  and add (add_out, icode[3], icode[2], icode[1], icode[0]);
  not not_3 (not_3_out, icode[2]);
  and mul (mul_out, icode[3], not_3_out, not_4_out, not_5_out);
  not not_4 (not_4_out, icode[1]);
  not not_5 (not_5_out, icode[0]);
  nor nor_1 (nor_1_out, out_6[0], out_6[1], out_6[2], out_6[3], out_6[4], out_6[5], out_6[6], out_6[7]);
  Register #(.width(1)) ZF (.D(nor_1_out), .en(ifun[1]), .Q(out_7), .clk(clock_1_out));  // open: clr
  Clock clock_1 (.out(clock_1_out));
  or u_val_A (val_A_out, add_out, mul_out);
  or or_1 (or_1_out, ld_out, st_out, add_out, mul_out);
  Multiplexer #(.width(8), .disabled(0), .enable("false")) multiplexer_1 (
    .in0(adder_1_out), .in1(multiplier_1_out), .out(out_6), .sel(ifun[0]));
  Adder adder_1 (.a(multiplexer_2_out), .b(val_B), .out(adder_1_out));  // open: cin, cout
  Multiplexer #(.width(8), .disabled(0)) multiplexer_2 (
    .in0(val_C), .in1(val_A), .out(multiplexer_2_out), .sel(val_A_out), .en(or_1_out));
  Multiplier multiplier_1 (.a(multiplexer_2_out), .b(val_B), .out(multiplier_1_out));  // open: cin, cout

  // Notes on the sheet:
  //   bit 0(right): 0 = add, 1 = multiply
  //   bit 1: 0 = don't update ZF, 1 = update ZF
endmodule

// Reg File
module Register_File (
  input  in_1,
  input  [3:0] in_2,
  input  in_3,
  input  [3:0] in_4,
  input  [7:0] in_5,
  input  in_6,
  input  [3:0] in_7,
  output [7:0] out_8,
  output [7:0] out_9
);

  wire clock_1_out;
  wire [7:0] A_q, B_q, C_q, D_q, demultiplexer_2_out0, demultiplexer_2_out1, demultiplexer_2_out2,
       demultiplexer_2_out3, demultiplexer_2_out4, demultiplexer_2_out5, demultiplexer_2_out6,
       demultiplexer_2_out7, demultiplexer_2_out8, demultiplexer_2_out9, demultiplexer_2_out10,
       demultiplexer_2_out11, demultiplexer_2_out12, demultiplexer_2_out13, demultiplexer_2_out14,
       demultiplexer_2_out15, E_q, F_q, G_q, H_q, I_q, J_q, K_q, L_q, M_q, N_q, rbp_q, rsp_q;
  wire [15:0] demultiplexer_1_out0;

  Demultiplexer #(.select(4), .enable("false")) demultiplexer_1 (
    .out0(demultiplexer_1_out0[0]), .out1(demultiplexer_1_out0[1]), .out2(demultiplexer_1_out0[2]),
    .out3(demultiplexer_1_out0[3]), .out4(demultiplexer_1_out0[4]), .out5(demultiplexer_1_out0[5]),
    .out6(demultiplexer_1_out0[6]), .out7(demultiplexer_1_out0[7]), .out8(demultiplexer_1_out0[8]),
    .out9(demultiplexer_1_out0[9]), .out10(demultiplexer_1_out0[10]), .out11(demultiplexer_1_out0[11]),
    .out12(demultiplexer_1_out0[12]), .out13(demultiplexer_1_out0[13]), .out14(demultiplexer_1_out0[14]),
    .out15(demultiplexer_1_out0[15]), .in(in_6), .sel(in_7));
  Demultiplexer #(.select(4), .width(8), .disabled(0)) demultiplexer_2 (
    .out0(demultiplexer_2_out0), .out1(demultiplexer_2_out1), .out2(demultiplexer_2_out2),
    .out3(demultiplexer_2_out3), .out4(demultiplexer_2_out4), .out5(demultiplexer_2_out5),
    .out6(demultiplexer_2_out6), .out7(demultiplexer_2_out7), .out8(demultiplexer_2_out8),
    .out9(demultiplexer_2_out9), .out10(demultiplexer_2_out10), .out11(demultiplexer_2_out11),
    .out12(demultiplexer_2_out12), .out13(demultiplexer_2_out13), .out14(demultiplexer_2_out14),
    .out15(demultiplexer_2_out15), .in(in_5), .sel(in_7), .en(in_6));
  Clock clock_1 (.out(clock_1_out));
  Register A (.D(demultiplexer_2_out0), .en(demultiplexer_1_out0[0]), .Q(A_q), .clk(clock_1_out));  // open: clr
  Register B (.D(demultiplexer_2_out1), .en(demultiplexer_1_out0[1]), .Q(B_q), .clk(clock_1_out));  // open: clr
  Register C (.D(demultiplexer_2_out2), .en(demultiplexer_1_out0[2]), .Q(C_q), .clk(clock_1_out));  // open: clr
  Register D (.D(demultiplexer_2_out3), .en(demultiplexer_1_out0[3]), .Q(D_q), .clk(clock_1_out));  // open: clr
  Register E (.D(demultiplexer_2_out4), .en(demultiplexer_1_out0[4]), .Q(E_q), .clk(clock_1_out));  // open: clr
  Register F (.D(demultiplexer_2_out5), .en(demultiplexer_1_out0[5]), .Q(F_q), .clk(clock_1_out));  // open: clr
  Register G (.D(demultiplexer_2_out6), .en(demultiplexer_1_out0[6]), .Q(G_q), .clk(clock_1_out));  // open: clr
  Register H (.D(demultiplexer_2_out7), .en(demultiplexer_1_out0[7]), .Q(H_q), .clk(clock_1_out));  // open: clr
  Register I (.D(demultiplexer_2_out8), .en(demultiplexer_1_out0[8]), .Q(I_q), .clk(clock_1_out));  // open: clr
  Register J (.D(demultiplexer_2_out9), .en(demultiplexer_1_out0[9]), .Q(J_q), .clk(clock_1_out));  // open: clr
  Register K (.D(demultiplexer_2_out10), .en(demultiplexer_1_out0[10]), .Q(K_q), .clk(clock_1_out));  // open: clr
  Register L (.D(demultiplexer_2_out11), .en(demultiplexer_1_out0[11]), .Q(L_q), .clk(clock_1_out));  // open: clr
  Register M (.D(demultiplexer_2_out12), .en(demultiplexer_1_out0[12]), .Q(M_q), .clk(clock_1_out));  // open: clr
  Register N (.D(demultiplexer_2_out13), .en(demultiplexer_1_out0[13]), .Q(N_q), .clk(clock_1_out));  // open: clr
  Register rbp (.D(demultiplexer_2_out14), .en(demultiplexer_1_out0[14]), .Q(rbp_q), .clk(clock_1_out));  // open: clr
  Register rsp (.D(demultiplexer_2_out15), .en(demultiplexer_1_out0[15]), .Q(rsp_q), .clk(clock_1_out));  // open: clr
  Multiplexer #(.select(4), .width(8), .disabled(0)) multiplexer_1 (
    .in0(A_q), .in1(B_q), .in2(C_q), .in3(D_q), .in4(E_q), .in5(F_q), .in6(G_q), .in7(H_q), .in8(I_q),
    .in9(J_q), .in10(K_q), .in11(L_q), .in12(M_q), .in13(N_q), .in14(rbp_q), .in15(rsp_q), .out(out_8),
    .sel(in_2), .en(in_1));
  Multiplexer #(.select(4), .width(8), .disabled(0)) multiplexer_2 (
    .in0(A_q), .in1(B_q), .in2(C_q), .in3(D_q), .in4(E_q), .in5(F_q), .in6(G_q), .in7(H_q), .in8(I_q),
    .in9(J_q), .in10(K_q), .in11(L_q), .in12(M_q), .in13(N_q), .in14(rbp_q), .in15(rsp_q), .out(out_9),
    .sel(in_4), .en(in_3));
endmodule

module Memory (
  input  [7:0] Address_Bus,
  input  [7:0] in_2,
  input  [3:0] icode,
  output [7:0] Data_Bus
);

  wire clock_1_out, not_1_out, not_2_out, or_1_out, read_out, write_out;
  wire [7:0] ram_1_data, register_1_q;

  not not_1 (not_1_out, icode[1]);
  not not_2 (not_2_out, icode[0]);
  Register register_1 (.D(Address_Bus), .Q(register_1_q), .clk(clock_1_out));  // open: en, clr
  and read (read_out, icode[3], icode[2], not_1_out, icode[0]);
  and write (write_out, icode[3], icode[2], icode[1], not_2_out);
  Clock clock_1 (.out(clock_1_out));
  or or_1 (or_1_out, write_out, read_out);
  RAM #(.bus("separate")) ram_1 (
    .addr(register_1_q), .din(in_2), .data(ram_1_data), .str(write_out), .sel(or_1_out), .clk(clock_1_out),
    .ld(read_out));  // open: clr
  Register register_2 (.D(ram_1_data), .Q(Data_Bus), .clk(clock_1_out));  // open: en, clr

  // Notes on the sheet:
  //   00 - Do Nothing
  //   01 - Read
  //   10 - Write
  //   Data_in
  //   RAM
  //   ROM
endmodule

module Write_Back (
  input  [7:0] in_1,
  input  [7:0] in_2,
  input  [7:0] in_3,
  input  [3:0] icode,
  input  cnd,
  output [7:0] out_6
);

  wire _0001_out, _0010_out, _0011_out, _0100_out, _0111_2_out, _0111_out, _1000_out, _1101_out, _1110_out,
       _1111_out;
  wire [1:0] or_1_out;

  and _0100 (_0100_out, ~icode[0], ~icode[1], icode[2], ~icode[3]);  // AND_Gate
  and _0011 (_0011_out, icode[0], icode[1], ~icode[2], ~icode[3]);  // AND_Gate
  or or_1 (or_1_out[0], _0100_out, _0011_out, _1101_out, _1110_out, _1000_out, _1111_out, _0111_out, _0111_2_out, _0010_out);
  and _1101 (_1101_out, icode[0], ~icode[1], icode[2], icode[3]);  // AND_Gate
  and _1110 (_1110_out, ~icode[0], icode[1], icode[2], icode[3]);  // AND_Gate
  and _1000 (_1000_out, ~icode[0], ~icode[1], ~icode[2]);  // AND_Gate
  and _1111 (_1111_out, icode[0], icode[1], icode[2], icode[3]);
  Multiplexer #(.select(2), .width(8)) multiplexer_1 (
    .in1(in_1), .in2(in_2), .in3(in_3), .out(out_6), .sel(or_1_out));  // open: in0, en
  and _0111 (_0111_out, icode[0], icode[1], ~cnd, icode[2], ~icode[3]);  // AND_Gate
  or or_2 (or_1_out[1], _0111_2_out, _0010_out, _0001_out);
  and _0111_2 (_0111_2_out, icode[0], icode[1], cnd, icode[2], ~icode[3]);  // AND_Gate
  and _0010 (_0010_out, ~icode[0], icode[1], ~icode[2], ~icode[3]);  // AND_Gate
  and _0001 (_0001_out, icode[0], ~icode[1], ~icode[2], ~icode[3]);  // AND_Gate

  // Notes on the sheet:
  //   INPUTS
  //   01 ValP
  //   10 ValM
  //   11 ValC
  //   icode:
  //   irmov - 11
  //   rrmovl - 100
  //   ld - 1101
  //   st -1110
  //   jmp - 111
  //   halt - 0
  //   add - 1111
  //   mul - 1000
  //   call - 10
  //   return - 1
  //   PC <- valP
  //   PC <- valP
  //   PC <- valP
  //   PC <- valP
  //   PC <- valP
  //   PC <- valP
  //   PC <- valC
  //   PC <- valM
  //   PC <- cond ? valC : val P
  //   10 valM = 0001
  //   11 valC = 0010 + 0111*cnd
  //   01 valP = 0011 + 0100 + 1101 + 1110 + 0111*cnd' + 1111 + 1000 
endmodule

module Val_A_B_enabler (
  input  [3:0] icode,
  output enabler
);

  wire add_out, ld_out, mul_out, not_1_out, not_2_out, not_3_out, not_4_out, not_5_out, not_6_out, not_7_out,
       not_8_out, rrmov_out, st_out;

  not not_1 (not_1_out, icode[0]);
  not not_2 (not_2_out, icode[1]);
  not not_3 (not_3_out, icode[2]);
  not not_4 (not_4_out, icode[1]);
  not not_5 (not_5_out, icode[0]);
  not not_6 (not_6_out, icode[3]);
  not not_7 (not_7_out, icode[1]);
  not not_8 (not_8_out, icode[0]);
  and st (st_out, icode[3], icode[2], icode[1], not_1_out);
  and ld (ld_out, icode[3], icode[2], not_2_out, icode[0]);
  and add (add_out, icode[3], icode[2], icode[1], icode[0]);
  and mul (mul_out, icode[3], not_3_out, not_4_out, not_5_out);
  and rrmov (rrmov_out, not_6_out, icode[2], not_7_out, not_8_out);
  or or_1 (enabler, st_out, ld_out, add_out, mul_out, rrmov_out);
endmodule

module Register_Write_Decoder (
  input  [3:0] icode,
  input  [3:0] rA,
  input  [3:0] rB,
  input  [7:0] val_M,
  input  [7:0] val_E,
  input  [7:0] val_A,
  input  [7:0] val_C,
  output write_enable,
  output [3:0] register,
  output [7:0] write_data
);

  wire add_out, irmov_out, ld_out, mul_out, not_1_out, not_2_out, not_3_out, not_4_out, not_5_out, not_6_out,
       not_7_out, not_8_out, not_9_out, rrmov_out, write_rB_out;
  wire [1:0] b_c_e_out;

  not not_1 (not_1_out, icode[1]);
  not not_2 (not_2_out, icode[2]);
  not not_3 (not_3_out, icode[1]);
  not not_4 (not_4_out, icode[0]);
  not not_5 (not_5_out, icode[3]);
  not not_6 (not_6_out, icode[1]);
  not not_7 (not_7_out, icode[0]);
  not not_8 (not_8_out, icode[3]);
  not not_9 (not_9_out, icode[2]);
  and ld (ld_out, icode[3], icode[2], not_1_out, icode[0]);
  and add (add_out, icode[3], icode[2], icode[1], icode[0]);
  and mul (mul_out, icode[3], not_2_out, not_3_out, not_4_out);
  and rrmov (rrmov_out, not_5_out, icode[2], not_6_out, not_7_out);
  and irmov (irmov_out, not_8_out, not_9_out, icode[1], icode[0]);
  or b_c_e (b_c_e_out[0], add_out, mul_out, irmov_out);
  or d_e (b_c_e_out[1], rrmov_out, irmov_out);
  Multiplexer #(.select(2), .width(8), .disabled(0)) multiplexer_1 (
    .in0(val_M), .in1(val_E), .in2(val_A), .in3(val_C), .out(write_data), .sel(b_c_e_out), .en(write_enable));
  or write_rB (write_rB_out, add_out, mul_out, rrmov_out);
  Multiplexer #(.width(4), .disabled(0)) multiplexer_2 (
    .in0(rA), .in1(rB), .out(register), .sel(write_rB_out), .en(write_enable));
  or or_1 (write_enable, ld_out, add_out, mul_out, rrmov_out, irmov_out);
endmodule
